# Fritzing sketch neo-biped (saved by Fritzing 0.9.4)

parts:
  LED2 = LED - 5mm [color="Red (633nm)" package="5 mm [THT]"]
  LED3 = LED - 5mm [color="Red (633nm)" package="5 mm [THT]"]
  M1 = Mega2560 R3 Pro Mini
  U1 = LM2596 step down module
  U2 = LM2596 step down module
  VCC1 = 4 x AAA Battery Mount
  S1 = Taiway 100-SP-X-T1 SPDT Miniature Toggle Switch [part_number=100-SP-X-T1-0-0-B1-M1 package=THT]
  J2 = Basic Servo
  J3 = Basic Servo
  J4 = Basic Servo
  J5 = Basic Servo
  J6 = Basic Servo
  J7 = Basic Servo
  J8 = Basic Servo
  J9 = Basic Servo
  J10 = Basic Servo
  J11 = Basic Servo
  J13 = Basic Servo
  J14 = Basic Servo
  J15 = Basic Servo
  J16 = Basic Servo
  J17 = Basic Servo
  J18 = Basic Servo
  J19 = Basic Servo
  J20 = Basic Servo
  J12 = Basic Servo

nets:
  N1: LED2.cathode, LED3.cathode, M1.GND-1, M1.GND-2, U1.IN-, U1.OUT-, U2.IN-, U2.OUT-, J12.gnd
  N2: LED2.anode, LED3.anode, M1.46
  N3: M1.3▀, J8.pulse
  N4: M1.5▀, J10.pulse
  N5: M1.7▀, J5.pulse
  N6: M1.9▀, J15.pulse
  N7: M1.11▀, J17.pulse
  N8: M1.13▀, J19.pulse
  N9: M1.15, J3.pulse
  N10: M1.17, J11.pulse
  N11: M1.19, J20.pulse
  N12: M1.20, J12.pulse
  N13: M1.18, J13.pulse
  N14: M1.16, J4.pulse
  N15: M1.14, J2.pulse
  N16: M1.12▀, J18.pulse
  N17: M1.10▀, J16.pulse
  N18: M1.8▀, J14.pulse
  N19: M1.6▀, J6.pulse
  N20: M1.4▀, J9.pulse
  N21: M1.2▀, J7.pulse
  N22: M1.5V-2, U2.OUT+
  N23: U1.IN+, U2.IN+
  N24: U1.OUT+, J12.vcc
  N25: VCC1.+, S1.COM

custom parts:
  Mega2560 R3 Pro Mini: The Mega 2560 R3 Pro Mini :- Completely compatible with original Arduino Mega2560 Pin pitch: 0.1 inch Size: 5.42cm*3.68cm With Atmega16U2 chip as the USB to Serial converter 5V working voltage. Input Voltage:7-12V Analog Input Pins: 16 Digital I/O pins: 54 The Mega 2560 R3 Pro Mini has no datasheet and no info and I don't have one to compare, so I made this based on photos. Use it at your own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
  LM2596 step down module: LM2596 DC-DC step down power supply module 3 A.
